// Logisim project buildMux.circ as structural Verilog
module _2_1_MUX (
  input  in_1,
  input  in_2,
  input  in_3,
  output out_4
);

  wire and_1_out, and_2_out, not_1_out;

  not not_1 (not_1_out, in_3);
  and and_1 (and_1_out, in_1, not_1_out);
  or or_1 (out_4, and_1_out, and_2_out);
  and and_2 (and_2_out, in_2, in_3);
endmodule

module _4_1_MUX (
  input  in_00,
  input  in_01,
  input  in_10,
  input  in_11,
  input  sel_0,
  input  sel_1,
  output out
);

  wire n2_1_mux_1_out_4, n2_1_mux_2_out_4;

  _2_1_MUX u_2_1_mux_1 (.in_1(in_00), .in_2(in_01), .in_3(sel_1), .out_4(n2_1_mux_1_out_4));
  _2_1_MUX u_2_1_mux_2 (.in_1(in_10), .in_2(in_11), .in_3(sel_1), .out_4(n2_1_mux_2_out_4));
  _2_1_MUX u_2_1_mux_3 (.in_1(n2_1_mux_1_out_4), .in_2(n2_1_mux_2_out_4), .in_3(sel_0), .out_4(out));
endmodule
