// Logisim project verify.circ as structural Verilog: 7 circuits, main circuit tester
module simple (
  output [1:0] a,
  output [1:0] b,
  output [2:0] sum,
  output halt
);

  wire clock_1_out;

  Clock clock_1 (.out(clock_1_out));
  Counter #(.width(4), .max('hf)) counter_1 (.Q({b, a}), .carry(halt), .clk(clock_1_out));  // open: load, D, count, clr
  _2_bit u_2_bit_1 (.a(a), .b(b), .sum(sum));
endmodule

module tester (
  output same,
  output halt
);

  wire clock_1_out;
  wire [2:0] master_1_sum, query_1_out_3;
  wire [3:0] counter_1_q;

  Clock clock_1 (.out(clock_1_out));
  Counter #(.width(4), .max('hf)) counter_1 (
    .Q(counter_1_q), .carry(halt), .clk(clock_1_out));  // open: load, D, count, clr
  master master_1 (.a(counter_1_q[1:0]), .b(counter_1_q[3:2]), .sum(master_1_sum));
  query query_1 (.in_1(counter_1_q[1:0]), .in_2(counter_1_q[3:2]), .out_3(query_1_out_3));
  Comparator #(.width(3)) comparator_1 (.a(master_1_sum), .b(query_1_out_3), .eq(same));  // open: gt, lt
endmodule

module _2_bit (
  input  [1:0] a,
  input  [1:0] b,
  output [2:0] sum
);

  Adder #(.width(2)) adder_1 (.a(a), .b(b), .out(sum[1:0]), .cout(sum[2]));  // open: cin
endmodule

module master (
  input  [1:0] a,
  input  [1:0] b,
  output [2:0] sum
);

  Adder #(.width(2)) adder_1 (.a(a), .b(b), .out(sum[1:0]), .cout(sum[2]));  // open: cin
endmodule

// soln
module query (
  input  [1:0] in_1,
  input  [1:0] in_2,
  output [2:0] out_3
);

  half_adder half_adder_1 (.a(in_1[0]), .b(in_2[0]), .sum(out_3[0]));  // open: carry
  full_adder full_adder_1 (.a(in_1[1]), .b(in_2[1]), .carry(out_3[2]), .sum(out_3[1]));  // open: c
endmodule

// HA
module half_adder (
  input  a,
  input  b,
  output sum,
  output carry
);

  wire and_2_out, and_3_out, not_1_out, not_2_out;

  and and_1 (sum, a, b);
  not not_1 (not_1_out, a);
  not not_2 (not_2_out, b);
  and and_2 (and_2_out, not_1_out, b);
  and and_3 (and_3_out, a, not_2_out);
  or or_1 (carry, and_2_out, and_3_out);
endmodule

// FA
module full_adder (
  input  a,
  input  b,
  input  c,
  output sum,
  output carry
);

  wire and_2_out, and_3_out, and_4_out, and_5_out, not_1_out, not_2_out, not_3_out, not_4_out, not_5_out,
       not_6_out, or_1_out, or_2_out, or_3_out;

  or or_1 (or_1_out, a, b);
  or or_2 (or_2_out, a, c);
  or or_3 (or_3_out, b, c);
  not not_1 (not_1_out, a);
  not not_2 (not_2_out, b);
  not not_3 (not_3_out, a);
  not not_4 (not_4_out, c);
  not not_5 (not_5_out, b);
  not not_6 (not_6_out, c);
  and and_1 (sum, or_1_out, or_2_out, or_3_out);
  and and_2 (and_2_out, not_1_out, not_2_out, c);
  and and_3 (and_3_out, not_3_out, b, not_4_out);
  and and_4 (and_4_out, a, not_5_out, not_6_out);
  and and_5 (and_5_out, a, b, c);
  or or_4 (carry, and_2_out, and_3_out, and_4_out, and_5_out);
endmodule
