// Logisim project verify.circ as structural Verilog: 8 circuits, main circuit tester
module simple (
  output [1:0] a,
  output [1:0] b,
  output [2:0] sum,
  output halt
);

  wire clock_1_out;

  Clock clock_1 (.out(clock_1_out));
  Counter #(.width(4), .max('hf)) counter_1 (.Q({b, a}), .carry(halt), .clk(clock_1_out));  // open: load, D, count, clr
  _2_bit u_2_bit_1 (.a(a), .b(b), .sum(sum));
endmodule

module tester (
  output same,
  output halt
);

  wire clock_1_out;
  wire [2:0] master_1_sum, query_1_out_3;
  wire [3:0] counter_1_q;

  Clock clock_1 (.out(clock_1_out));
  Counter #(.width(4), .max('hf)) counter_1 (
    .Q(counter_1_q), .carry(halt), .clk(clock_1_out));  // open: load, D, count, clr
  master master_1 (.a(counter_1_q[1:0]), .b(counter_1_q[3:2]), .sum(master_1_sum));
  query query_1 (.in_1(counter_1_q[1:0]), .in_2(counter_1_q[3:2]), .out_3(query_1_out_3));
  Comparator #(.width(3)) comparator_1 (.a(master_1_sum), .b(query_1_out_3), .eq(same));  // open: gt, lt
endmodule

module _2_bit (
  input  [1:0] a,
  input  [1:0] b,
  output [2:0] sum
);

  Adder #(.width(2)) adder_1 (.a(a), .b(b), .out(sum[1:0]), .cout(sum[2]));  // open: cin
endmodule

module master (
  input  [1:0] a,
  input  [1:0] b,
  output [2:0] sum
);

  Adder #(.width(2)) adder_1 (.a(a), .b(b), .out(sum[1:0]), .cout(sum[2]));  // open: cin
endmodule

// soln
module query (
  input  [1:0] in_1,
  input  [1:0] in_2,
  output [2:0] out_3
);

  half_adder half_adder_1 (.a(in_1[0]), .b(in_2[0]), .sum(out_3[0]));  // open: carry
  full_adder full_adder_1 (.a(in_1[1]), .b(in_2[1]), .carry_2(out_3[2]), .sum(out_3[1]));  // open: carry
endmodule

// HA
module half_adder (
  input  a,
  input  b,
  output carry,
  output sum
);

  wire and_2_out, and_3_out, not_1_out, not_2_out;

  and and_1 (carry, a, b);
  not not_1 (not_1_out, a);
  not not_2 (not_2_out, b);
  and and_2 (and_2_out, not_1_out, b);
  and and_3 (and_3_out, a, not_2_out);
  or or_1 (sum, and_2_out, and_3_out);
endmodule

// FA
module full_adder (
  input  a,
  input  b,
  input  carry,
  output carry_2,
  output sum
);

  wire and_2_out, and_3_out, and_4_out, and_5_out, not_1_out, not_2_out, not_3_out, not_4_out, not_5_out,
       not_6_out, or_1_out, or_2_out, or_3_out;

  or or_1 (or_1_out, a, b);
  or or_2 (or_2_out, a, carry);
  or or_3 (or_3_out, b, carry);
  not not_1 (not_1_out, a);
  not not_2 (not_2_out, b);
  not not_3 (not_3_out, a);
  not not_4 (not_4_out, carry);
  not not_5 (not_5_out, b);
  not not_6 (not_6_out, carry);
  and and_1 (carry_2, or_1_out, or_2_out, or_3_out);
  and and_2 (and_2_out, not_1_out, not_2_out, carry);
  and and_3 (and_3_out, not_3_out, b, not_4_out);
  and and_4 (and_4_out, a, not_5_out, not_6_out);
  and and_5 (and_5_out, a, b, carry);
  or or_4 (sum, and_2_out, and_3_out, and_4_out, and_5_out);
endmodule

// FA
module full_adder__sum_of_products (
  input  a,
  input  b,
  input  carry,
  output carry_2,
  output sum
);

  wire and_1_out, and_2_out, and_3_out, and_4_out, and_5_out, and_6_out, and_7_out, not_1_out, not_2_out,
       not_3_out, not_4_out, not_5_out, not_6_out;

  and and_1 (and_1_out, b, carry);
  and and_2 (and_2_out, a, carry);
  and and_3 (and_3_out, a, b);
  not not_1 (not_1_out, a);
  not not_2 (not_2_out, b);
  not not_3 (not_3_out, a);
  not not_4 (not_4_out, carry);
  not not_5 (not_5_out, b);
  not not_6 (not_6_out, carry);
  or or_1 (carry_2, and_1_out, and_2_out, and_3_out);
  and and_4 (and_4_out, not_1_out, not_2_out, carry);
  and and_5 (and_5_out, not_3_out, b, not_4_out);
  and and_6 (and_6_out, a, not_5_out, not_6_out);
  and and_7 (and_7_out, a, b, carry);
  or or_2 (sum, and_4_out, and_5_out, and_6_out, and_7_out);
endmodule
